# Fritzing sketch ADXL345Breadboard (saved by Fritzing 0.9.3b)
circuit board: 3.85907cm x 2.76566cm
breadboards: 1

parts:
  ADXL345 = Triple Axis Accelerometer Breakout - ADXL345
  Header = double row female pin header, 6 pins [form="♀ (female)"]

nets:
  N1: ADXL345.GND, Header.pin1
  N2: ADXL345.VCC, Header.pin4
  N3: ADXL345.SDA, Header.pin5
  N4: ADXL345.SCL, Header.pin6

notes:
  Thomas Aziz
